# Fritzing sketch joystick (saved by Fritzing 0.9.3b)
circuit board: 5.53402cm x 7.91721cm

parts:
  IC1 = 74LS38 [chip_label=IC package="DIP (Dual Inline) [THT]"]
  IC1_PWR = 74LS38 [package="DIP (Dual Inline) [THT]"]
  IC1_4 = 74LS38 [package="DIP (Dual Inline) [THT]"]
  IC1_3 = 74LS38 [package="DIP (Dual Inline) [THT]"]
  IC1_2 = 74LS38 [package="DIP (Dual Inline) [THT]"]
  IC1_1 = 74LS38 [package="DIP (Dual Inline) [THT]"]
  Alimentation = female pin header, 2 pins [form="♀ (female)"]
  R1 = Resistor [tolerance=±5% resistance=1k package=THT]
  IC2 = 74LS38 [chip_label=IC package="DIP (Dual Inline) [THT]"]
  IC2_PWR = 74LS38 [package="DIP (Dual Inline) [THT]"]
  IC2_4 = 74LS38 [package="DIP (Dual Inline) [THT]"]
  IC2_3 = 74LS38 [package="DIP (Dual Inline) [THT]"]
  IC2_2 = 74LS38 [package="DIP (Dual Inline) [THT]"]
  IC2_1 = 74LS38 [package="DIP (Dual Inline) [THT]"]
  MH-ET_LIVE_ESP32_DEVKIT1 = MH-ET LIVE ESP32 DEVKIT 38 pins
  Amstrad = female pin header, 7 pins [form="♀ (female)"]

nets:
  Common: IC1.connector0, IC1.connector1, IC1_1.pin1, IC1_1.pin2, Amstrad.pin2
  N1: IC1.connector2, IC1.connector3, IC1.connector8, IC1.connector11, IC1_4.pin12, IC1_3.pin9, IC1_2.pin4, IC1_1.pin3, R1.Pin_1, IC2.connector0, IC2.connector3, IC2.connector8, IC2_3.pin9, IC2_2.pin4, IC2_1.pin1
  UC_Fire1: IC1.connector4, IC1_2.pin5, MH-ET_LIVE_ESP32_DEVKIT1.IO32
  Fire1: IC1.connector5, IC1_2.pin6, Amstrad.pin1
  GND: IC1.connector6, IC1_PWR.pin7, Alimentation.pin2, IC2.connector6, IC2.connector10, IC2.connector11, IC2.connector12, IC2_PWR.pin7, IC2_4.pin11, IC2_4.pin12, IC2_4.pin13, MH-ET_LIVE_ESP32_DEVKIT1.GND#64
  Fire2: IC1.connector7, IC1_3.pin8, Amstrad.pin4
  UC_Fire2: IC1.connector9, IC1_3.pin10, MH-ET_LIVE_ESP32_DEVKIT1.IO33
  Up: IC1.connector10, IC1_4.pin11, Amstrad.pin3
  UC_Up: IC1.connector12, IC1_4.pin13, MH-ET_LIVE_ESP32_DEVKIT1.IO25
  5V: IC1.connector13, IC1_PWR.pin14, Alimentation.pin1, R1.Pin_0, IC2.connector13, IC2_PWR.pin14, MH-ET_LIVE_ESP32_DEVKIT1.5V
  UC_Down: IC2.connector1, IC2_1.pin2, MH-ET_LIVE_ESP32_DEVKIT1.IO26
  Down: IC2.connector2, IC2_1.pin3, Amstrad.pin6
  UC_Left: IC2.connector4, IC2_2.pin5, MH-ET_LIVE_ESP32_DEVKIT1.IO27
  Left: IC2.connector5, IC2_2.pin6, Amstrad.pin5
  Right: IC2.connector7, IC2_3.pin8, Amstrad.pin7
  UC_Right: IC2.connector9, IC2_3.pin10, MH-ET_LIVE_ESP32_DEVKIT1.IO14

custom parts:
  74LS38: 74LS38 AND Gate
  74LS38: 74LS38 AND Gate
  74LS38: 74LS38 AND Gate
  74LS38: 74LS38 AND Gate
  74LS38: 74LS38 AND Gate
  74LS38: 74LS38 AND Gate
  MH-ET LIVE ESP32 DEVKIT 38 pins: http://mh.nodebb.com/topic/2/mh-et-live-esp32-devkit
